// Logisim project cpu.circ as structural Verilog: 2 circuits, main circuit main
module main (
  input  [15:0] INSTRUCTION,
  input  CLOCK,
  output [15:0] FETCH_ADDRESS,
  output [15:0] L_s0_Value_7c9fba82,
  output [15:0] L_s1_Value_2cb75696,
  output [15:0] L_s2_Value_be7b1681,
  output [15:0] L_ra_Value_55886cf9,
  output [15:0] L_sp_Value_a0856b3d,
  output [15:0] L_HI_Value_3bde5b98,
  output [15:0] L_LO_Value_b62659ce
);

  wire [15:0] HI, LO, PC;

  Register #(.width(16)) L_PC_bd1e00e6 (.Q(PC));  // open: D, en, clk, clr
  Register #(.width(16)) L_LO_ba622f5d (.Q(LO));  // open: D, en, clk, clr
  Register #(.width(16)) L_HI_1d3f3066 (.Q(HI));  // open: D, en, clk, clr
  // alu_main main_1: pin names not known
  regfile_main main_2 (
    .L_s0_Value_3e1de553(L_s0_Value_7c9fba82), .L_s1_Value_f16d02bf(L_s1_Value_2cb75696),
    .L_s2_Value_6a9ed51f(L_s2_Value_be7b1681), .L_ra_Value_b804995d(L_ra_Value_55886cf9),
    .L_sp_Value_269f0ffd(L_sp_Value_a0856b3d));  // open: Read_Data_1_c47ea0d8, Read_Data_2_34b29906, Read_Register_1_eca808b4, Read_Register_2_4b336a3e, Write_Register_1c78e1ef, Write_Data_00073c80, Write_Enable_5f560963, Clock
  // mem_main MEM: pin names not known
  CONTROL_UNIT_CPU control_unit_cpu_1 (
    .INSTR(INSTRUCTION), .PC(PC));  // open: WRITE_EN_RAM, WRITE_EN_REG, ALU_SWITCH, ALU_X, ALU_Y, RAM_ADDR_R, RAM_ADDR_WR, REG_ADDR_R1, REG_ADDR_R2, REG_ADDR_WR

  // Other names for the same wires on the sheet: clk = CLOCK; fetch_addr[15:0] = FETCH_ADDRESS

  // Notes on the sheet:
  //   Output
  //   These are outputs/inputs from run.circ
  //   Inputs
  //   These are DEBUG/TEST outputs from your circuit.
endmodule

module CONTROL_UNIT_CPU (
  input  [15:0] INSTR,
  input  [15:0] PC,
  output WRITE_EN_RAM,
  output WRITE_EN_REG,
  output [2:0] ALU_SWITCH,
  output [15:0] ALU_X,
  output [15:0] ALU_Y,
  output [15:0] RAM_ADDR_R,
  output [15:0] RAM_ADDR_WR,
  output [2:0] REG_ADDR_R1,
  output [2:0] REG_ADDR_R2,
  output [2:0] REG_ADDR_WR
);

  wire demultiplexer_1_out0, demultiplexer_2_out0;

  Demultiplexer #(.select(4), .enable("false")) demultiplexer_1 (
    .out0(demultiplexer_1_out0), .in(1'b1), .sel(INSTR[15:12]));  // open: out1, out2, out3, out4, out5, out6, out7, out8, out9, out10, out11, out12, out13, out14, out15
  Demultiplexer #(.select(3), .enable("false")) demultiplexer_2 (
    .out0(demultiplexer_2_out0), .in(demultiplexer_1_out0), .sel(INSTR[2:0]));  // open: out1, out2, out3, out4, out5, out6, out7
  Multiplexer #(.width(16), .enable("false")) multiplexer_1 (
    .in0({{10{1'b0}}, INSTR[5:0]}), .out(ALU_Y), .sel(demultiplexer_1_out0));  // open: in1

  // Notes on the sheet:
  //   SELECT OPCODE
  //   0 = type R
  //   SELECT FUNCT
  //   SLL
  //   On r-type,  X is rs and Y is rt
endmodule
